# Fritzing sketch Prototype (saved by Fritzing 0.9.3b)
breadboards: 1

parts:
  Part1 = Arduino Pro Mini (3.3V)  # not connected
  LED1 = LED - 5mm [color="Infrared (850nm)" package="5 mm [THT]"]
  Part3 = Infra red receiver
  R1 = Resistor [tolerance=±20% resistance=560 package="2512 [SMD]"]
  Q1 = NPN-Transistor [package="TO92 [THT]"]
  Q1_2 = PNP-Transistor [package="SOT-23 [SMD]"]
  LED2 = LED - 5mm [color="Red (633nm)" package="5 mm [THT]"]
  R2 = Resistor [tolerance=±5% resistance=220 package=THT]

nets:
  N1: LED1.cathode, Q1.E, Q1_2.2
  N2: LED1.anode, Part3.VCC
  N3: Part3.GND, Q1.C, Q1_2.1, R2.Pin_1
  N4: R1.Pin_1, Q1.B, Q1_2.0
  N5: LED2.cathode, R2.Pin_0
